// Logisim project clock.circ as structural Verilog: 1 circuit, main circuit main
module main (
  input  in_1
);

  wire digital_oscilloscope_1_p2, digital_oscilloscope_1_p3, digital_oscilloscope_1_p4,
       digital_oscilloscope_2_p1, digital_oscilloscope_2_p2, digital_oscilloscope_2_p3,
       digital_oscilloscope_2_p4, n7447_1_pin9, n7447_1_pin10, n7447_1_pin11, n7447_1_pin12, n7447_1_pin13,
       n7447_1_pin14, n7447_1_pin15, n7474_1_pin2, n7474_1_pin5, n7474_1_pin12, n7474_2_pin2, n7474_2_pin5,
       n7474_2_pin12, n7474_3_pin2, n7474_3_pin5, n7474_3_pin12, n74161_1_pin7, nand_1_out;

  // Digital_Oscilloscope #(.nState(25)) digital_oscilloscope_1: pin names not known; wires that end beside it: in_1, digital_oscilloscope_1_p2, digital_oscilloscope_1_p3, digital_oscilloscope_1_p4
  _7474 u_7474_1 (
    .pin2(n7474_1_pin2), .pin3(in_1), .pin5(n7474_1_pin5), .pin6(n7474_1_pin2), .pin12(n7474_1_pin12),
    .pin11(n7474_1_pin5), .pin9(digital_oscilloscope_1_p2), .pin8(n7474_1_pin12));  // open: pin1, pin4, pin13, pin10
  // Digital_Oscilloscope digital_oscilloscope_2: pin names not known; wires that end beside it: digital_oscilloscope_2_p1, digital_oscilloscope_2_p2, digital_oscilloscope_2_p3, digital_oscilloscope_2_p4
  nand nand_1 (nand_1_out, digital_oscilloscope_2_p4, digital_oscilloscope_2_p2);
  _74161 u_74161_1 (
    .pin1(nand_1_out), .pin2(in_1), .pin7(n74161_1_pin7), .pin14(digital_oscilloscope_2_p1),
    .pin13(digital_oscilloscope_2_p2), .pin12(digital_oscilloscope_2_p3), .pin11(digital_oscilloscope_2_p4),
    .pin10(n74161_1_pin7), .pin9(n74161_1_pin7));  // open: pin3, pin4, pin5, pin6, pin15
  _7474 u_7474_2 (
    .pin2(n7474_2_pin2), .pin3(digital_oscilloscope_1_p2), .pin5(n7474_2_pin5), .pin6(n7474_2_pin2),
    .pin12(n7474_2_pin12), .pin11(n7474_2_pin5), .pin9(digital_oscilloscope_1_p3), .pin8(n7474_2_pin12));  // open: pin1, pin4, pin13, pin10
  _7474 u_7474_3 (
    .pin2(n7474_3_pin2), .pin3(digital_oscilloscope_1_p3), .pin5(n7474_3_pin5), .pin6(n7474_3_pin2),
    .pin12(n7474_3_pin12), .pin11(n7474_3_pin5), .pin9(digital_oscilloscope_1_p4), .pin8(n7474_3_pin12));  // open: pin1, pin4, pin13, pin10
  _7447 u_7447_1 (
    .pin1(digital_oscilloscope_2_p2), .pin2(digital_oscilloscope_2_p3), .pin6(digital_oscilloscope_2_p4),
    .pin7(digital_oscilloscope_2_p1), .pin15(n7447_1_pin15), .pin14(n7447_1_pin14), .pin13(n7447_1_pin13),
    .pin12(n7447_1_pin12), .pin11(n7447_1_pin11), .pin10(n7447_1_pin10), .pin9(n7447_1_pin9));  // open: pin3, pin4, pin5
  _7_Segment_Display u_7_segment_display_1 (
    .g(n7447_1_pin14), .f(n7447_1_pin15), .a(n7447_1_pin13), .b(n7447_1_pin12), .e(n7447_1_pin9),
    .d(n7447_1_pin10), .c(n7447_1_pin11));  // open: dp
  // also tied to VCC on the sheet: n74161_1_pin7
endmodule
