// Logisim project clock_v2.circ as structural Verilog: 1 circuit, main circuit main
module main (
  input  in_1
);

  wire digital_oscilloscope_1_p2, digital_oscilloscope_1_p3, digital_oscilloscope_1_p4,
       digital_oscilloscope_2_p2, digital_oscilloscope_2_p3, digital_oscilloscope_2_p4,
       digital_oscilloscope_2_p5, n7447_1_pin9, n7447_1_pin10, n7447_1_pin11, n7447_1_pin12, n7447_1_pin13,
       n7447_1_pin14, n7447_1_pin15, n7447_2_pin9, n7447_2_pin10, n7447_2_pin11, n7447_2_pin12,
       n7447_2_pin13, n7447_2_pin14, n7447_2_pin15, n74161_1_pin7, n74161_2_pin7, n74161_3_pin7,
       n74161_4_pin7, n74161_4_pin11, n74161_4_pin12, n74161_4_pin13, n74161_4_pin14, n74161_5_pin7,
       nand_1_out, nand_2_out, not_1_out, not_2_out;

  // Digital_Oscilloscope #(.nState(25)) digital_oscilloscope_1: pin names not known; wires that end beside it: in_1, digital_oscilloscope_1_p2, digital_oscilloscope_1_p3, digital_oscilloscope_1_p4
  _74161 u_74161_1 (
    .pin2(in_1), .pin7(n74161_1_pin7), .pin11(digital_oscilloscope_1_p2), .pin10(n74161_1_pin7));  // open: pin1, pin3, pin4, pin5, pin6, pin15, pin14, pin13, pin12, pin9
  nand nand_1 (nand_1_out, digital_oscilloscope_2_p5, digital_oscilloscope_2_p3);
  // Digital_Oscilloscope digital_oscilloscope_2: pin names not known; wires that end beside it: in_1, digital_oscilloscope_2_p2, digital_oscilloscope_2_p3, digital_oscilloscope_2_p4, digital_oscilloscope_2_p5
  _74161 u_74161_2 (
    .pin1(nand_1_out), .pin2(in_1), .pin7(n74161_2_pin7), .pin14(digital_oscilloscope_2_p2),
    .pin13(digital_oscilloscope_2_p3), .pin12(digital_oscilloscope_2_p4), .pin11(digital_oscilloscope_2_p5),
    .pin10(n74161_2_pin7), .pin9(n74161_2_pin7));  // open: pin3, pin4, pin5, pin6, pin15
  not not_1 (not_1_out, digital_oscilloscope_1_p2);
  nand nand_2 (nand_2_out, n74161_4_pin13, n74161_4_pin12);
  not not_2 (not_2_out, nand_1_out);
  _74161 u_74161_3 (
    .pin2(not_1_out), .pin7(n74161_3_pin7), .pin11(digital_oscilloscope_1_p3), .pin10(n74161_3_pin7),
    .pin9(n74161_3_pin7));  // open: pin1, pin3, pin4, pin5, pin6, pin15, pin14, pin13, pin12
  _74161 u_74161_4 (
    .pin1(nand_2_out), .pin2(not_2_out), .pin7(n74161_4_pin7), .pin14(n74161_4_pin14),
    .pin13(n74161_4_pin13), .pin12(n74161_4_pin12), .pin11(n74161_4_pin11), .pin10(n74161_4_pin7),
    .pin9(n74161_4_pin7));  // open: pin3, pin4, pin5, pin6, pin15
  _74161 u_74161_5 (
    .pin7(n74161_5_pin7), .pin10(n74161_5_pin7), .pin9(n74161_5_pin7));  // open: pin1, pin2, pin3, pin4, pin5, pin6, pin15, pin14, pin13, pin12, pin11
  _7447 u_7447_1 (
    .pin1(digital_oscilloscope_2_p3), .pin2(digital_oscilloscope_2_p4), .pin6(digital_oscilloscope_2_p5),
    .pin7(digital_oscilloscope_2_p2), .pin15(n7447_1_pin15), .pin14(n7447_1_pin14), .pin13(n7447_1_pin13),
    .pin12(n7447_1_pin12), .pin11(n7447_1_pin11), .pin10(n7447_1_pin10), .pin9(n7447_1_pin9));  // open: pin3, pin4, pin5
  _7_Segment_Display u_7_segment_display_1 (
    .g(n7447_1_pin14), .f(n7447_1_pin15), .a(n7447_1_pin13), .b(n7447_1_pin12), .e(n7447_1_pin9),
    .d(n7447_1_pin10), .c(n7447_1_pin11));  // open: dp
  _7447 u_7447_2 (
    .pin1(n74161_4_pin13), .pin2(n74161_4_pin12), .pin6(n74161_4_pin11), .pin7(n74161_4_pin14),
    .pin15(n7447_2_pin15), .pin14(n7447_2_pin14), .pin13(n7447_2_pin13), .pin12(n7447_2_pin12),
    .pin11(n7447_2_pin11), .pin10(n7447_2_pin10), .pin9(n7447_2_pin9));  // open: pin3, pin4, pin5
  _7_Segment_Display u_7_segment_display_2 (
    .g(n7447_2_pin14), .f(n7447_2_pin15), .a(n7447_2_pin13), .b(n7447_2_pin12), .e(n7447_2_pin9),
    .d(n7447_2_pin10), .c(n7447_2_pin11));  // open: dp
  // also tied to VCC on the sheet: {n74161_1_pin7, n74161_2_pin7, n74161_3_pin7, n74161_4_pin7, n74161_5_pin7}
endmodule
