// Logisim project clock_v3.circ as structural Verilog: 1 circuit, main circuit main
module main (
);

  wire and_1_out, and_2_out, and_3_out, clock_1_out, n7447_1_pin9, n7447_1_pin10, n7447_1_pin11,
       n7447_1_pin12, n7447_1_pin13, n7447_1_pin14, n7447_1_pin15, n7447_2_pin9, n7447_2_pin10,
       n7447_2_pin11, n7447_2_pin12, n7447_2_pin13, n7447_2_pin14, n7447_2_pin15, n7447_3_pin9,
       n7447_3_pin10, n7447_3_pin11, n7447_3_pin12, n7447_3_pin13, n7447_3_pin14, n7447_3_pin15,
       n7447_4_pin9, n7447_4_pin10, n7447_4_pin11, n7447_4_pin12, n7447_4_pin13, n7447_4_pin14,
       n7447_4_pin15, n7447_5_pin9, n7447_5_pin10, n7447_5_pin11, n7447_5_pin12, n7447_5_pin13,
       n7447_5_pin14, n7447_5_pin15, n7447_6_pin9, n7447_6_pin10, n7447_6_pin11, n7447_6_pin12,
       n7447_6_pin13, n7447_6_pin14, n7447_6_pin15, n74163_1_pin7, n74163_2_pin2, n74163_3_pin2,
       n74163_4_pin11, n74163_5_pin2, n74163_6_pin11, n74163_7_pin11, n74163_9_pin2, nor_1_out, nor_2_out,
       not_1_out, not_2_out;
  wire [3:0] n7447_1_pin7, n7447_2_pin7, n7447_3_pin7, n7447_4_pin7, n7447_5_pin7, n7447_6_pin7;

  _7447 u_7447_1 (
    .pin1(n7447_1_pin7[1]), .pin2(n7447_1_pin7[2]), .pin6(n7447_1_pin7[3]), .pin7(n7447_1_pin7[0]),
    .pin15(n7447_1_pin15), .pin14(n7447_1_pin14), .pin13(n7447_1_pin13), .pin12(n7447_1_pin12),
    .pin11(n7447_1_pin11), .pin10(n7447_1_pin10), .pin9(n7447_1_pin9));  // open: pin3, pin4, pin5
  nor nor_1 (nor_1_out, and_1_out, and_3_out);
  not not_1 (not_1_out, n7447_1_pin7[1]);
  _74163 #(.ShowInternalStructure("true")) u_74163_1 (
    .pin1(not_1_out), .pin2(nor_1_out), .pin7(n74163_1_pin7), .pin14(n7447_1_pin7[0]),
    .pin13(n7447_1_pin7[1]), .pin12(n7447_1_pin7[2]), .pin11(n7447_1_pin7[3]), .pin10(n74163_1_pin7),
    .pin9(n74163_1_pin7));  // open: pin3, pin4, pin5, pin6, pin15
  _7_Segment_Display u_7_segment_display_1 (
    .g(n7447_1_pin14), .f(n7447_1_pin15), .a(n7447_1_pin13), .b(n7447_1_pin12), .e(n7447_1_pin9),
    .d(n7447_1_pin10), .c(n7447_1_pin11));  // open: dp
  and and_1 (and_1_out, and_2_out, n7447_1_pin7[1]);
  nor nor_2 (nor_2_out, and_1_out, and_3_out);
  _7_Segment_Display u_7_segment_display_2 (
    .g(n7447_2_pin14), .f(n7447_2_pin15), .a(n7447_2_pin13), .b(n7447_2_pin12), .e(n7447_2_pin9),
    .d(n7447_2_pin10), .c(n7447_2_pin11));  // open: dp
  _7447 u_7447_2 (
    .pin1(n7447_2_pin7[1]), .pin2(n7447_2_pin7[2]), .pin6(n7447_2_pin7[3]), .pin7(n7447_2_pin7[0]),
    .pin15(n7447_2_pin15), .pin14(n7447_2_pin14), .pin13(n7447_2_pin13), .pin12(n7447_2_pin12),
    .pin11(n7447_2_pin11), .pin10(n7447_2_pin10), .pin9(n7447_2_pin9));  // open: pin3, pin4, pin5
  and and_2 (and_2_out, not_2_out, n7447_2_pin7[1], n7447_2_pin7[0]);
  and and_3 (and_3_out, n7447_2_pin7[0], n7447_2_pin7[3]);
  _74163 #(.ShowInternalStructure("true")) u_74163_2 (
    .pin1(nor_2_out), .pin2(n74163_2_pin2), .pin7(n74163_1_pin7), .pin14(n7447_2_pin7[0]),
    .pin13(n7447_2_pin7[1]), .pin12(n7447_2_pin7[2]), .pin11(n7447_2_pin7[3]), .pin10(n74163_1_pin7),
    .pin9(n74163_1_pin7));  // open: pin3, pin4, pin5, pin6, pin15
  not not_2 (not_2_out, n7447_2_pin7[3]);
  _7447 u_7447_3 (
    .pin1(n7447_3_pin7[1]), .pin2(n7447_3_pin7[2]), .pin6(n7447_3_pin7[3]), .pin7(n7447_3_pin7[0]),
    .pin15(n7447_3_pin15), .pin14(n7447_3_pin14), .pin13(n7447_3_pin13), .pin12(n7447_3_pin12),
    .pin11(n7447_3_pin11), .pin10(n7447_3_pin10), .pin9(n7447_3_pin9));  // open: pin3, pin4, pin5
  nand nand_1 (n74163_2_pin2, n7447_3_pin7[0], n7447_3_pin7[2]);
  _74163 #(.ShowInternalStructure("true")) u_74163_3 (
    .pin1(n74163_2_pin2), .pin2(n74163_3_pin2), .pin7(n74163_1_pin7), .pin14(n7447_3_pin7[0]),
    .pin13(n7447_3_pin7[1]), .pin12(n7447_3_pin7[2]), .pin11(n7447_3_pin7[3]), .pin10(n74163_1_pin7),
    .pin9(n74163_1_pin7));  // open: pin3, pin4, pin5, pin6, pin15
  _74163 u_74163_4 (
    .pin7(n74163_1_pin7), .pin11(n74163_4_pin11), .pin10(n74163_1_pin7), .pin9(n74163_1_pin7));  // open: pin1, pin2, pin3, pin4, pin5, pin6, pin15, pin14, pin13, pin12
  _7_Segment_Display u_7_segment_display_3 (
    .g(n7447_3_pin14), .f(n7447_3_pin15), .a(n7447_3_pin13), .b(n7447_3_pin12), .e(n7447_3_pin9),
    .d(n7447_3_pin10), .c(n7447_3_pin11));  // open: dp
  _7_Segment_Display u_7_segment_display_4 (
    .g(n7447_4_pin14), .f(n7447_4_pin15), .a(n7447_4_pin13), .b(n7447_4_pin12), .e(n7447_4_pin9),
    .d(n7447_4_pin10), .c(n7447_4_pin11));  // open: dp
  _7447 u_7447_4 (
    .pin1(n7447_4_pin7[1]), .pin2(n7447_4_pin7[2]), .pin6(n7447_4_pin7[3]), .pin7(n7447_4_pin7[0]),
    .pin15(n7447_4_pin15), .pin14(n7447_4_pin14), .pin13(n7447_4_pin13), .pin12(n7447_4_pin12),
    .pin11(n7447_4_pin11), .pin10(n7447_4_pin10), .pin9(n7447_4_pin9));  // open: pin3, pin4, pin5
  nand nand_2 (n74163_3_pin2, n7447_4_pin7[0], n7447_4_pin7[3]);
  _74163 #(.ShowInternalStructure("true")) u_74163_5 (
    .pin1(n74163_3_pin2), .pin2(n74163_5_pin2), .pin7(n74163_1_pin7), .pin14(n7447_4_pin7[0]),
    .pin13(n7447_4_pin7[1]), .pin12(n7447_4_pin7[2]), .pin11(n7447_4_pin7[3]), .pin10(n74163_1_pin7),
    .pin9(n74163_1_pin7));  // open: pin3, pin4, pin5, pin6, pin15
  _74163 u_74163_6 (
    .pin2(n74163_4_pin11), .pin7(n74163_1_pin7), .pin11(n74163_6_pin11), .pin10(n74163_1_pin7),
    .pin9(n74163_1_pin7));  // open: pin1, pin3, pin4, pin5, pin6, pin15, pin14, pin13, pin12
  _74163 u_74163_7 (
    .pin2(n74163_6_pin11), .pin7(n74163_1_pin7), .pin11(n74163_7_pin11), .pin10(n74163_1_pin7),
    .pin9(n74163_1_pin7));  // open: pin1, pin3, pin4, pin5, pin6, pin15, pin14, pin13, pin12
  _7447 u_7447_5 (
    .pin1(n7447_5_pin7[1]), .pin2(n7447_5_pin7[2]), .pin6(n7447_5_pin7[3]), .pin7(n7447_5_pin7[0]),
    .pin15(n7447_5_pin15), .pin14(n7447_5_pin14), .pin13(n7447_5_pin13), .pin12(n7447_5_pin12),
    .pin11(n7447_5_pin11), .pin10(n7447_5_pin10), .pin9(n7447_5_pin9));  // open: pin3, pin4, pin5
  nand nand_3 (n74163_5_pin2, n7447_5_pin7[0], n7447_5_pin7[2]);
  _74163 u_74163_8 (
    .pin2(n74163_7_pin11), .pin7(n74163_1_pin7), .pin10(n74163_1_pin7), .pin9(n74163_1_pin7));  // open: pin1, pin3, pin4, pin5, pin6, pin15, pin14, pin13, pin12, pin11
  _7_Segment_Display u_7_segment_display_5 (
    .g(n7447_5_pin14), .f(n7447_5_pin15), .a(n7447_5_pin13), .b(n7447_5_pin12), .e(n7447_5_pin9),
    .d(n7447_5_pin10), .c(n7447_5_pin11));  // open: dp
  _74163 #(.ShowInternalStructure("true")) u_74163_9 (
    .pin1(n74163_5_pin2), .pin2(n74163_9_pin2), .pin7(n74163_1_pin7), .pin14(n7447_5_pin7[0]),
    .pin13(n7447_5_pin7[1]), .pin12(n7447_5_pin7[2]), .pin11(n7447_5_pin7[3]), .pin10(n74163_1_pin7),
    .pin9(n74163_1_pin7));  // open: pin3, pin4, pin5, pin6, pin15
  Clock clock_1 (.out(clock_1_out));
  _7_Segment_Display u_7_segment_display_6 (
    .g(n7447_6_pin14), .f(n7447_6_pin15), .a(n7447_6_pin13), .b(n7447_6_pin12), .e(n7447_6_pin9),
    .d(n7447_6_pin10), .c(n7447_6_pin11));  // open: dp
  nand nand_4 (n74163_9_pin2, n7447_6_pin7[0], n7447_6_pin7[3]);
  _7447 u_7447_6 (
    .pin1(n7447_6_pin7[1]), .pin2(n7447_6_pin7[2]), .pin6(n7447_6_pin7[3]), .pin7(n7447_6_pin7[0]),
    .pin15(n7447_6_pin15), .pin14(n7447_6_pin14), .pin13(n7447_6_pin13), .pin12(n7447_6_pin12),
    .pin11(n7447_6_pin11), .pin10(n7447_6_pin10), .pin9(n7447_6_pin9));  // open: pin3, pin4, pin5
  _74163 #(.ShowInternalStructure("true")) u_74163_10 (
    .pin1(n74163_9_pin2), .pin2(clock_1_out), .pin7(n74163_1_pin7), .pin14(n7447_6_pin7[0]),
    .pin13(n7447_6_pin7[1]), .pin12(n7447_6_pin7[2]), .pin11(n7447_6_pin7[3]), .pin10(n74163_1_pin7),
    .pin9(n74163_1_pin7));  // open: pin3, pin4, pin5, pin6, pin15
  // also tied to VCC on the sheet: n74163_1_pin7

  // Notes on the sheet:
  //   1 Hz
endmodule
